# Fritzing sketch fritzing-schematic (saved by Fritzing 0.9.3b)
breadboards: 1

parts:
  LED1 = Patrick's LED driver [package="5 mm [THT]"]
  Part1 = Arduino Uno (Rev3)
  Part2 = JeePlug experimenter's board
  R1 = Resistor [tolerance=±5% resistance=220 package=THT]
  Part3 = Real Time Clock Module - DS1307 RTC Breakout Board
  U1 = SWITCH-4PDT [package=switch-4pdt-cnk]

nets (from the breadboard view):
  VCC: LED1.vcc, Part1.VIN
  N1: LED1.en, Part1.D9_PWM, R1.Pin_1
  GND: LED1.gnd, Part1.GND, Part2.N$26, Part3.GND
  N2: Part1.A0, Part2.A3
  N3: Part1.A1, Part2.A4
  N4: Part1.A4/SDA, Part3.SDA
  N5: Part1.A5/SCL, Part3.SCL
  N6: Part1.D8, U1.1
  N7: Part1.D10_PWM/SS, Part2.A6
  N8: Part1.D11_PWM/MOSI, Part2.A2
  N9: Part1.D12/MISO, Part2.A1
  N10: Part1.D13/SCK, Part2.N$24
  N11: Part1.D2, U1.7
  N12: Part1.D3_PWM, U1.6
  N13: Part1.D4, U1.5
  N14: Part1.D5_PWM, U1.4
  N15: Part1.D6_PWM, U1.3
  N16: Part1.D7, U1.2
  N17: Part1.3V3, Part2.A5
  5V: Part1.5V, R1.Pin_0, Part3.5V

notes:
  NOKIA 3310 Display
  1 - RST@ 13
  2 - CE @ 12
  3 - DC @ 11
  4 - DIN @ A0
  5 - CLK @ A1
  6 - VCC
  7 - LIGHT
  8 - GND
  KEYPAD
  1 2 3
  4 5 6
  7 8 9
  * 0 #

custom parts:
  Patrick's LED driver: LED driver based off silly led part for convenience
